# Fritzing sketch chonBot-2WD (saved by Fritzing 0.9.6b)

parts:
  Motor_DC_Esquerdo1 = Motor DC 6V Esquerdo
  MOTOR_DC_6V_direito1 = MOTOR_DC6V
  Componente1 = Arduino Uno (Rev3) - ICSP
  MCU1 = Raspberry Pi Zero  # not connected
  USBTTL1 = Micro USB B Plug
  Componente3 = OTG [package=THT]  # not connected
  USBTTL3 = USB A Plug
  U1 = TCRT5000 [package=THT]
  U2 = TCRT5000 [package=THT]
  R1 = Resistor [tolerance=±5% resistance=330 package="1206 [SMD]"]
  R2 = Resistor [tolerance=±5% resistance=1k package="1206 [SMD]"]
  R3 = Resistor [tolerance=±5% resistance=1k package="1206 [SMD]"]
  LED1 = smd LED [color="Red (633nm)" package="1206 [SMD]"]
  LED2 = smd LED [color="Red (633nm)" package="1206 [SMD]"]
  R4 = Resistor [tolerance=±5% resistance=330 package="1206 [SMD]"]
  LED3 = smd LED [color="White (4500K)" package="0805 [SMD]"]
  LED4 = smd LED [color="White (4500K)" package="0805 [SMD]"]
  R5 = Resistor [tolerance=±5% resistance=330 package="1206 [SMD]"]
  LED5 = smd LED [color="Red (633nm)" package="0805 [SMD]"]
  LED6 = smd LED [color="Green (560nm)" package="0805 [SMD]"]
  R6 = Resistor [tolerance=±5% resistance=330 package="1206 [SMD]"]
  HC-SR04_Sensor_1 = HC-SR04 Ultrasonic Distance Sensor
  R7 = Photocell (LDR) [package=THT]
  R8 = Resistor [tolerance=±5% resistance=1k package="1206 [SMD]"]
  S2 = H-Bridge with L298N
  R9 = Resistor [tolerance=±5% resistance=330 package="1206 [SMD]"]
  Componente8 = PowerBank 5v 5000mAh
  Componente9 = PowerBank 5v 5000mAh
  Q2 = Basic FET P-Channel [package="TO220 [THT]"]  # not connected
  USBTTL5 = miicroUSB TTL Serial Cable
  Mod1 = Passive Buzzer

nets:
  N1: Motor_DC_Esquerdo1.GND, S2.OUT4-Motor2
  N2: Motor_DC_Esquerdo1.VCC, S2.OUT3-Motor2
  N3: MOTOR_DC_6V_direito1.GND, S2.OUT1-Motor1
  N4: MOTOR_DC_6V_direito1.VCC, S2.OUT2-Motor1
  N5: Componente1.A0, R7.pin_0, R8.Pin_1
  N6: Componente1.A1, U2.Pin_1, R2.Pin_0
  N7: Componente1.A2, U1.Pin_1, R3.Pin_1
  N8: Componente1.ICSP_MOSI, Componente1.D11_PWM/MOSI, Mod1.S
  N9: Componente1.D8, HC-SR04_Sensor_1.TRIG
  N10: Componente1.D9_PWM, S2.IN3
  N11: Componente1.D10_PWM/SS, S2.IN4
  N12: Componente1.D12/MISO, R6.Pin_0
  GND: Componente1.GND, U1.Pin_2, U1.Pin_3, U2.Pin_2, U2.Pin_3, LED1.anode, LED2.anode, LED3.anode, LED4.anode, LED5.anode, LED6.anode, HC-SR04_Sensor_1.GND, R7.pin_1, S2.GND, Componente8.negative, Mod1.-
  N13: Componente1.D2, R4.Pin_1
  N14: Componente1.D3_PWM, R5.Pin_0
  N15: Componente1.D4, R9.Pin_0
  N16: Componente1.D5_PWM, S2.IN1
  N17: Componente1.D6_PWM, S2.IN2
  N18: Componente1.D7, HC-SR04_Sensor_1.ECHO
  5V: Componente1.5V, R1.Pin_1, R2.Pin_1, R3.Pin_0, HC-SR04_Sensor_1.VCC, R8.Pin_0
  N19: USBTTL1.usb, USBTTL3.usb
  N20: U1.Pin_4, U2.Pin_4, R1.Pin_0
  N21: LED1.cathode, LED2.cathode, R4.Pin_0
  N22: LED3.cathode, LED4.cathode, R5.Pin_1
  N23: LED5.cathode, R6.Pin_1
  N24: LED6.cathode, R9.Pin_1
  N25: S2.12V, Componente8.positive
  N26: Componente9.positive, USBTTL5.5V
  N27: Componente9.negative, USBTTL5.GND

custom parts:
  Motor DC 6V Esquerdo: Motor dc esquerdo
  MOTOR_DC6V: Motor dc 6V direito
  TCRT5000: TCRT5000 optical reflective sensor
  H-Bridge with L298N: h-bridge
  Basic FET P-Channel: A MOSFET P-Channel Transistor
  miicroUSB TTL Serial Cable: USB TTL Serial Cable
